// Logisim project Advanced_computer.circ as structural Verilog: 1 circuit, main circuit main
module main (
  input  in_1,
  input  in_2
);

  wire clock_1_out, clock_2_out, undriven;
  wire [6:0] keyboard_1_data, keyboard_2_data;

  Keyboard keyboard_1 (.clk(clock_1_out), .clr(in_1), .data(keyboard_1_data));  // open: re, avail
  Clock clock_1 (.out(clock_1_out));
  Clock clock_2 (.out(clock_2_out));
  Keyboard keyboard_2 (.clk(clock_2_out), .clr(in_2), .data(keyboard_2_data));  // open: re, avail
  TTY tty_1 (.data(keyboard_1_data), .clk(clock_1_out), .we(undriven), .clr(in_1));
  TTY #(.rows(1)) tty_2 (.data(keyboard_2_data), .clk(clock_2_out), .clr(in_2));  // open: we
endmodule
