// Logisim project Computer.circ as structural Verilog
// Main
module CPU (
  input  in_1,
  output Error
);

  wire clock_1_out, instruction_register_1_out_18, instruction_register_1_out_19,
       instruction_register_1_out_20, instruction_register_1_out_21, pc_1_out_3, pc_1_out_4, pc_1_out_5,
       pc_1_out_6, pc_1_out_7, pc_1_out_8, pc_1_out_9, pc_1_out_10, pc_1_out_11, pc_1_out_12, pc_1_out_13,
       pc_1_out_14, pc_1_out_15, pc_1_out_16, pc_1_out_17, pc_1_out_18, pc_1_out_19, pc_1_out_20,
       pc_1_out_21, pc_1_out_22, pc_1_out_23, pc_1_out_24, pc_1_out_25, program_rom_1_out_17,
       program_rom_1_out_18, program_rom_1_out_19, program_rom_1_out_20, program_rom_1_out_21,
       program_rom_1_out_22, program_rom_1_out_23, program_rom_1_out_24;

  Clock clock_1 (.out(clock_1_out));
  PC pc_1 (
    .in_1(in_1), .in_2(clock_1_out), .out_22(pc_1_out_22), .out_23(pc_1_out_23), .out_24(pc_1_out_24),
    .out_25(pc_1_out_25), .out_19(pc_1_out_19), .out_20(pc_1_out_20), .out_21(pc_1_out_21),
    .out_5(pc_1_out_5), .out_7(pc_1_out_7), .out_9(pc_1_out_9), .out_11(pc_1_out_11), .out_13(pc_1_out_13),
    .out_15(pc_1_out_15), .out_17(pc_1_out_17), .out_3(pc_1_out_3), .out_6(pc_1_out_6), .out_8(pc_1_out_8),
    .out_10(pc_1_out_10), .out_12(pc_1_out_12), .out_14(pc_1_out_14), .out_16(pc_1_out_16),
    .out_18(pc_1_out_18), .out_4(pc_1_out_4));
  Program_ROM program_rom_1 (
    .in_1(pc_1_out_3), .in_2(pc_1_out_4), .in_3(pc_1_out_5), .in_4(pc_1_out_6), .in_5(pc_1_out_7),
    .in_6(pc_1_out_8), .in_7(pc_1_out_9), .in_8(pc_1_out_10), .in_9(pc_1_out_11), .in_10(pc_1_out_12),
    .in_11(pc_1_out_13), .in_12(pc_1_out_14), .in_13(pc_1_out_15), .in_14(pc_1_out_16), .in_15(pc_1_out_17),
    .in_16(pc_1_out_18), .out_17(program_rom_1_out_17), .out_18(program_rom_1_out_18),
    .out_19(program_rom_1_out_19), .out_20(program_rom_1_out_20), .out_21(program_rom_1_out_21),
    .out_22(program_rom_1_out_22), .out_23(program_rom_1_out_23), .out_24(program_rom_1_out_24));
  instruction_register instruction_register_1 (
    .in_1(in_1), .in_4(program_rom_1_out_19), .in_5(program_rom_1_out_20), .in_6(program_rom_1_out_21),
    .in_7(program_rom_1_out_22), .in_8(program_rom_1_out_23), .in_9(program_rom_1_out_24),
    .in_2(program_rom_1_out_17), .in_3(program_rom_1_out_18), .in_12(pc_1_out_24), .in_13(pc_1_out_25),
    .in_10(pc_1_out_22), .in_11(pc_1_out_23), .out_16(Error), .out_17(Error),
    .out_18(instruction_register_1_out_18), .out_19(instruction_register_1_out_19),
    .out_20(instruction_register_1_out_20), .out_21(instruction_register_1_out_21), .out_14(Error),
    .out_15(Error));  // open: out_36, out_37, out_38, out_39, out_40, out_41, out_42, out_43, out_44, out_45, out_22, out_23, out_24, out_25, out_26, out_27, out_28, out_29, out_30, out_31, out_32, out_33, out_34, out_35
  Demux_1_16 demux_1_16_1 (
    .in_3(instruction_register_1_out_19), .in_2(instruction_register_1_out_20),
    .in_1(instruction_register_1_out_21), .in_4(instruction_register_1_out_18), .in_5(1'b1));  // open: out_7, out_8, out_9, out_10, out_11, out_12, out_13, out_14, out_15, out_16, out_17, out_18, out_19, out_20, out_21, out_6
endmodule

module Program_ROM (
  input  in_1,
  input  in_2,
  input  in_3,
  input  in_4,
  input  in_5,
  input  in_6,
  input  in_7,
  input  in_8,
  input  in_9,
  input  in_10,
  input  in_11,
  input  in_12,
  input  in_13,
  input  in_14,
  input  in_15,
  input  in_16,
  output out_17,
  output out_18,
  output out_19,
  output out_20,
  output out_21,
  output out_22,
  output out_23,
  output out_24
);

  ROM #(.addrWidth(16)) rom_1 (
    .addr({in_16, in_15, in_14, in_13, in_12, in_11, in_10, in_9, in_8, in_7, in_6, in_5, in_4, in_3, in_2, in_1}),
    .data({out_17, out_18, out_19, out_20, out_21, out_22, out_23, out_24}));

  // Notes on the sheet:
  //   contents of rom_1 (hex, n*v repeats v):
  //   1 2 3 4 5 6 7 8 9
endmodule

module ALU (
  input  in_1,
  input  in_2,
  input  in_3,
  input  in_4,
  input  in_5,
  input  in_6,
  input  in_7,
  input  in_8,
  input  in_9,
  input  in_10,
  input  in_11,
  input  in_12,
  input  in_13,
  input  in_14,
  input  in_15,
  input  in_16,
  input  in_17,
  input  in_18,
  input  in_19,
  input  in_20,
  input  in_21,
  output out_22,
  output out_23,
  output out_24,
  output out_25,
  output out_26,
  output out_27,
  output out_28,
  output out_29
);

  wire undriven, undriven_2, undriven_3, undriven_4, undriven_5, undriven_6, undriven_7, undriven_8,
       undriven_9, undriven_10, undriven_11, undriven_12, undriven_13, undriven_14, undriven_15, undriven_16;

  eight_bit_adder eight_bit_adder_1 (
    .in_1(undriven_15), .in_9(undriven_7), .in_2(undriven_14), .in_10(undriven_6), .in_8(undriven_16),
    .in_16(undriven_8), .in_3(undriven_13), .in_11(undriven_5), .in_4(undriven_12), .in_12(undriven_4),
    .in_5(undriven_11), .in_13(undriven_3), .in_6(undriven_10), .in_14(undriven_2), .in_7(undriven_9),
    .in_15(undriven));  // open: out_17, out_18, out_19, out_20, out_21, out_22, out_23, out_24
  eight_bit_subtractor eight_bit_subtractor_1 (
    .in_16(undriven_16), .in_8(undriven_8), .in_9(undriven_15), .in_1(undriven_7), .in_10(undriven_14),
    .in_2(undriven_6), .in_11(undriven_13), .in_3(undriven_5), .in_12(undriven_12), .in_4(undriven_4),
    .in_13(undriven_11), .in_5(undriven_3), .in_14(undriven_10), .in_6(undriven_2), .in_15(undriven_9),
    .in_7(undriven));  // open: out_23, out_24, out_17, out_18, out_19, out_20, out_21, out_22
  eight_bit_and eight_bit_and_1 (
    .in_1(undriven_8), .in_5(undriven_16), .in_9(undriven_4), .in_13(undriven_12), .in_2(undriven_7),
    .in_6(undriven_15), .in_10(undriven_3), .in_14(undriven_11), .in_3(undriven_6), .in_7(undriven_14),
    .in_11(undriven_2), .in_15(undriven_10), .in_4(undriven_5), .in_8(undriven_13), .in_12(undriven),
    .in_16(undriven_9));  // open: out_17, out_21, out_18, out_22, out_19, out_23, out_20, out_24
  eight_bit_or eight_bit_or_1 (
    .in_1(undriven_8), .in_5(undriven_16), .in_9(undriven_4), .in_13(undriven_12), .in_2(undriven_7),
    .in_6(undriven_15), .in_10(undriven_3), .in_14(undriven_11), .in_3(undriven_6), .in_7(undriven_14),
    .in_11(undriven_2), .in_15(undriven_10), .in_4(undriven_5), .in_8(undriven_13), .in_12(undriven),
    .in_16(undriven_9));  // open: out_17, out_21, out_18, out_22, out_19, out_23, out_20, out_24
  eight_bit_xor eight_bit_xor_1 (
    .in_1(undriven_8), .in_5(undriven_16), .in_9(undriven_4), .in_13(undriven_12), .in_2(undriven_7),
    .in_6(undriven_15), .in_10(undriven_3), .in_14(undriven_11), .in_3(undriven_6), .in_7(undriven_14),
    .in_11(undriven_2), .in_15(undriven_10), .in_4(undriven_5), .in_8(undriven_13), .in_12(undriven),
    .in_16(undriven_9));  // open: out_17, out_21, out_18, out_22, out_19, out_23, out_20, out_24

  // Other names for the same wires on the sheet: a1 = in_8; a2 = in_7; a3 = in_6; a4 = in_5; a5 = in_4; a6 = in_3;
  //   a7 = in_2; a8 = in_1; add = in_17; and = in_19; b1 = in_16; b2 = in_15; b3 = in_14; b4 = in_13; b5 = in_12;
  //   b6 = in_11; b7 = in_10; b8 = in_9; or = in_20; out_1_0d33bf7f = out_29; out_2_7d0e111c = out_28;
  //   out_3_304ffaf0 = out_27; out_4_221de9e4 = out_26; out_5_2785c5c8 = out_25; out_6_ac99cd26 = out_24;
  //   out_7_cf1fbdc8 = out_23; out_8_9c71e410 = out_22; sub = in_18; xor = in_21
endmodule

module half_adder (
  input  in_1,
  input  in_2,
  output out_3,
  output out_4
);

  and and_1 (out_4, in_1, in_2);
  xor xor_1 (out_3, in_1, in_2);
endmodule

module full_adder (
  input  in_1,
  input  in_2,
  input  in_3,
  output out_4,
  output out_5
);

  wire and_1_out, and_2_out, xor_1_out;

  xor xor_1 (xor_1_out, in_1, in_2);
  and and_1 (and_1_out, in_1, in_2);
  xor xor_2 (out_4, xor_1_out, in_3);
  and and_2 (and_2_out, xor_1_out, in_3);
  xor xor_3 (out_5, and_2_out, and_1_out);
endmodule

module half_subtractor (
  input  in_1,
  input  in_2,
  output out_3,
  output out_4
);

  wire not_1_out;

  not not_1 (not_1_out, in_1);
  xor xor_1 (out_3, in_1, in_2);
  and and_1 (out_4, not_1_out, in_2);
endmodule

module full_subtractor (
  input  in_1,
  input  in_2,
  input  in_3,
  output out_4,
  output out_5
);

  wire and_1_out, and_2_out, not_1_out, not_2_out, xor_1_out;

  xor xor_1 (xor_1_out, in_2, in_3);
  not not_1 (not_1_out, in_2);
  and and_1 (and_1_out, not_1_out, in_3);
  not not_2 (not_2_out, xor_1_out);
  xor xor_2 (out_4, in_1, xor_1_out);
  and and_2 (and_2_out, not_2_out, in_1);
  or or_1 (out_5, and_2_out, and_1_out);
endmodule

module eight_bit_adder (
  input  in_1,
  input  in_2,
  input  in_3,
  input  in_4,
  input  in_5,
  input  in_6,
  input  in_7,
  input  in_8,
  input  in_9,
  input  in_10,
  input  in_11,
  input  in_12,
  input  in_13,
  input  in_14,
  input  in_15,
  input  in_16,
  output out_17,
  output out_18,
  output out_19,
  output out_20,
  output out_21,
  output out_22,
  output out_23,
  output out_24
);

  wire full_adder_1_out_5, full_adder_2_out_5, full_adder_3_out_5, full_adder_4_out_5, full_adder_5_out_5,
       full_adder_6_out_5, half_adder_1_out_4;

  half_adder half_adder_1 (.in_1(in_8), .in_2(in_16), .out_4(half_adder_1_out_4), .out_3(out_24));
  full_adder full_adder_1 (
    .in_3(half_adder_1_out_4), .in_2(in_9), .in_1(in_1), .out_4(out_17), .out_5(full_adder_1_out_5));
  full_adder full_adder_2 (
    .in_3(full_adder_1_out_5), .in_2(in_10), .in_1(in_2), .out_4(out_18), .out_5(full_adder_2_out_5));
  full_adder full_adder_3 (
    .in_3(full_adder_2_out_5), .in_2(in_11), .in_1(in_3), .out_4(out_19), .out_5(full_adder_3_out_5));
  full_adder full_adder_4 (
    .in_3(full_adder_3_out_5), .in_2(in_12), .in_1(in_4), .out_4(out_20), .out_5(full_adder_4_out_5));
  full_adder full_adder_5 (
    .in_3(full_adder_4_out_5), .in_2(in_13), .in_1(in_5), .out_4(out_21), .out_5(full_adder_5_out_5));
  full_adder full_adder_6 (
    .in_3(full_adder_5_out_5), .in_2(in_14), .in_1(in_6), .out_4(out_22), .out_5(full_adder_6_out_5));
  full_adder full_adder_7 (.in_3(full_adder_6_out_5), .in_2(in_15), .in_1(in_7), .out_4(out_23));  // open: out_5
endmodule

module eight_bit_subtractor (
  input  in_1,
  input  in_2,
  input  in_3,
  input  in_4,
  input  in_5,
  input  in_6,
  input  in_7,
  input  in_8,
  input  in_9,
  input  in_10,
  input  in_11,
  input  in_12,
  input  in_13,
  input  in_14,
  input  in_15,
  input  in_16,
  output out_17,
  output out_18,
  output out_19,
  output out_20,
  output out_21,
  output out_22,
  output out_23,
  output out_24
);

  wire full_subtractor_1_out_5, full_subtractor_2_out_5, full_subtractor_3_out_5, full_subtractor_4_out_5,
       full_subtractor_5_out_5, full_subtractor_6_out_5, half_subtractor_1_out_4;

  half_subtractor half_subtractor_1 (.in_1(in_8), .in_2(in_16), .out_4(half_subtractor_1_out_4), .out_3(out_24));
  full_subtractor full_subtractor_1 (
    .in_3(in_9), .in_1(half_subtractor_1_out_4), .in_2(in_1), .out_4(out_17), .out_5(full_subtractor_1_out_5));
  full_subtractor full_subtractor_2 (
    .in_3(in_10), .in_1(full_subtractor_1_out_5), .in_2(in_2), .out_4(out_18), .out_5(full_subtractor_2_out_5));
  full_subtractor full_subtractor_3 (
    .in_3(in_11), .in_1(full_subtractor_2_out_5), .in_2(in_3), .out_4(out_19), .out_5(full_subtractor_3_out_5));
  full_subtractor full_subtractor_4 (
    .in_3(in_12), .in_1(full_subtractor_3_out_5), .in_2(in_4), .out_4(out_20), .out_5(full_subtractor_4_out_5));
  full_subtractor full_subtractor_5 (
    .in_3(in_13), .in_1(full_subtractor_4_out_5), .in_2(in_5), .out_4(out_21), .out_5(full_subtractor_5_out_5));
  full_subtractor full_subtractor_6 (
    .in_3(in_14), .in_1(full_subtractor_5_out_5), .in_2(in_6), .out_4(out_22), .out_5(full_subtractor_6_out_5));
  full_subtractor full_subtractor_7 (
    .in_3(in_15), .in_1(full_subtractor_6_out_5), .in_2(in_7), .out_4(out_23));  // open: out_5
endmodule

module eight_bit_and (
  input  in_1,
  input  in_2,
  input  in_3,
  input  in_4,
  input  in_5,
  input  in_6,
  input  in_7,
  input  in_8,
  input  in_9,
  input  in_10,
  input  in_11,
  input  in_12,
  input  in_13,
  input  in_14,
  input  in_15,
  input  in_16,
  output out_17,
  output out_18,
  output out_19,
  output out_20,
  output out_21,
  output out_22,
  output out_23,
  output out_24
);

  and and_1 (out_17, in_1, in_5);
  and and_2 (out_21, in_9, in_13);
  and and_3 (out_18, in_2, in_6);
  and and_4 (out_22, in_10, in_14);
  and and_5 (out_19, in_3, in_7);
  and and_6 (out_23, in_11, in_15);
  and and_7 (out_20, in_4, in_8);
  and and_8 (out_24, in_12, in_16);
endmodule

module eight_bit_or (
  input  in_1,
  input  in_2,
  input  in_3,
  input  in_4,
  input  in_5,
  input  in_6,
  input  in_7,
  input  in_8,
  input  in_9,
  input  in_10,
  input  in_11,
  input  in_12,
  input  in_13,
  input  in_14,
  input  in_15,
  input  in_16,
  output out_17,
  output out_18,
  output out_19,
  output out_20,
  output out_21,
  output out_22,
  output out_23,
  output out_24
);

  or or_1 (out_17, in_1, in_5);
  or or_2 (out_21, in_9, in_13);
  or or_3 (out_18, in_2, in_6);
  or or_4 (out_22, in_10, in_14);
  or or_5 (out_19, in_3, in_7);
  or or_6 (out_23, in_11, in_15);
  or or_7 (out_20, in_4, in_8);
  or or_8 (out_24, in_12, in_16);
endmodule

module eight_bit_xor (
  input  in_1,
  input  in_2,
  input  in_3,
  input  in_4,
  input  in_5,
  input  in_6,
  input  in_7,
  input  in_8,
  input  in_9,
  input  in_10,
  input  in_11,
  input  in_12,
  input  in_13,
  input  in_14,
  input  in_15,
  input  in_16,
  output out_17,
  output out_18,
  output out_19,
  output out_20,
  output out_21,
  output out_22,
  output out_23,
  output out_24
);

  xor xor_1 (out_17, in_1, in_5);
  xor xor_2 (out_21, in_9, in_13);
  xor xor_3 (out_18, in_2, in_6);
  xor xor_4 (out_22, in_10, in_14);
  xor xor_5 (out_19, in_3, in_7);
  xor xor_6 (out_23, in_11, in_15);
  xor xor_7 (out_20, in_4, in_8);
  xor xor_8 (out_24, in_12, in_16);
endmodule

module Counter (
  input  in_1,
  input  in_2,
  output out_3,
  output out_4,
  output out_5,
  output out_6,
  output out_7,
  output out_8,
  output out_9,
  output out_10,
  output out_11,
  output out_12,
  output out_13,
  output out_14,
  output out_15,
  output out_16,
  output out_17,
  output out_18
);

  wire clock_1_out, controlled_buffer_1_out, controlled_buffer_2_out, controlled_buffer_3_out,
       controlled_buffer_4_out, controlled_buffer_5_out, controlled_buffer_6_out, controlled_buffer_7_out,
       controlled_buffer_8_out, controlled_buffer_9_out, controlled_buffer_10_out, controlled_buffer_11_out,
       controlled_buffer_12_out, controlled_buffer_13_out, controlled_buffer_14_out,
       controlled_buffer_15_out, controlled_buffer_16_out, controlled_buffer_17_out, not_1_out, not_2_out,
       register_1_out_11, register_1_out_12, register_1_out_13, register_1_out_14, register_1_out_15,
       register_1_out_16, register_1_out_17, register_1_out_18, register_2_out_11, register_2_out_12,
       register_2_out_13, register_2_out_14, register_2_out_15, register_2_out_16, register_2_out_17,
       register_2_out_18, sixteen_bit_adder_1_out_18, sixteen_bit_adder_1_out_19, sixteen_bit_adder_1_out_20,
       sixteen_bit_adder_1_out_21, sixteen_bit_adder_1_out_22, sixteen_bit_adder_1_out_23,
       sixteen_bit_adder_1_out_24, sixteen_bit_adder_1_out_25, sixteen_bit_adder_1_out_26,
       sixteen_bit_adder_1_out_27, sixteen_bit_adder_1_out_28, sixteen_bit_adder_1_out_29,
       sixteen_bit_adder_1_out_30, sixteen_bit_adder_1_out_31, sixteen_bit_adder_1_out_32,
       sixteen_bit_adder_1_out_33;

  sixteen_bit_adder sixteen_bit_adder_1 (
    .in_9(out_12), .in_10(out_13), .in_11(out_14), .in_12(out_15), .in_13(out_16), .in_1(out_4),
    .in_14(out_17), .in_15(out_18), .in_2(out_5), .in_3(out_6), .in_17(in_2), .in_16(out_3), .in_4(out_7),
    .in_5(out_8), .in_6(out_9), .in_7(out_10), .in_8(out_11), .out_33(sixteen_bit_adder_1_out_33),
    .out_26(sixteen_bit_adder_1_out_26), .out_27(sixteen_bit_adder_1_out_27),
    .out_28(sixteen_bit_adder_1_out_28), .out_29(sixteen_bit_adder_1_out_29),
    .out_30(sixteen_bit_adder_1_out_30), .out_31(sixteen_bit_adder_1_out_31),
    .out_32(sixteen_bit_adder_1_out_32), .out_18(sixteen_bit_adder_1_out_18),
    .out_19(sixteen_bit_adder_1_out_19), .out_20(sixteen_bit_adder_1_out_20),
    .out_21(sixteen_bit_adder_1_out_21), .out_22(sixteen_bit_adder_1_out_22),
    .out_23(sixteen_bit_adder_1_out_23), .out_24(sixteen_bit_adder_1_out_24),
    .out_25(sixteen_bit_adder_1_out_25));
  assign controlled_buffer_1_out = in_1 ? 1'b0 : 1'bz;  // Controlled_Buffer controlled_buffer_1
  not not_1 (not_1_out, in_1);
  assign controlled_buffer_2_out = not_1_out ? sixteen_bit_adder_1_out_33 : 1'bz;  // Controlled_Buffer controlled_buffer_2
  buf buffer_1 (controlled_buffer_2_out, controlled_buffer_1_out);
  assign controlled_buffer_3_out = not_1_out ? sixteen_bit_adder_1_out_18 : 1'bz;  // Controlled_Buffer controlled_buffer_3
  buf buffer_2 (controlled_buffer_3_out, controlled_buffer_1_out);
  assign controlled_buffer_4_out = not_1_out ? sixteen_bit_adder_1_out_19 : 1'bz;  // Controlled_Buffer controlled_buffer_4
  buf buffer_3 (controlled_buffer_4_out, controlled_buffer_1_out);
  assign controlled_buffer_5_out = not_1_out ? sixteen_bit_adder_1_out_20 : 1'bz;  // Controlled_Buffer controlled_buffer_5
  buf buffer_4 (controlled_buffer_5_out, controlled_buffer_1_out);
  assign controlled_buffer_6_out = not_1_out ? sixteen_bit_adder_1_out_21 : 1'bz;  // Controlled_Buffer controlled_buffer_6
  buf buffer_5 (controlled_buffer_6_out, controlled_buffer_1_out);
  assign controlled_buffer_7_out = not_1_out ? sixteen_bit_adder_1_out_22 : 1'bz;  // Controlled_Buffer controlled_buffer_7
  buf buffer_6 (controlled_buffer_7_out, controlled_buffer_1_out);
  assign controlled_buffer_8_out = not_1_out ? sixteen_bit_adder_1_out_23 : 1'bz;  // Controlled_Buffer controlled_buffer_8
  buf buffer_7 (controlled_buffer_8_out, controlled_buffer_1_out);
  assign controlled_buffer_9_out = not_1_out ? sixteen_bit_adder_1_out_24 : 1'bz;  // Controlled_Buffer controlled_buffer_9
  buf buffer_8 (controlled_buffer_9_out, controlled_buffer_1_out);
  assign controlled_buffer_10_out = not_1_out ? sixteen_bit_adder_1_out_25 : 1'bz;  // Controlled_Buffer controlled_buffer_10
  buf buffer_9 (controlled_buffer_10_out, controlled_buffer_1_out);
  assign controlled_buffer_11_out = not_1_out ? sixteen_bit_adder_1_out_26 : 1'bz;  // Controlled_Buffer controlled_buffer_11
  buf buffer_10 (controlled_buffer_11_out, controlled_buffer_1_out);
  assign controlled_buffer_12_out = not_1_out ? sixteen_bit_adder_1_out_27 : 1'bz;  // Controlled_Buffer controlled_buffer_12
  buf buffer_11 (controlled_buffer_12_out, controlled_buffer_1_out);
  assign controlled_buffer_13_out = not_1_out ? sixteen_bit_adder_1_out_28 : 1'bz;  // Controlled_Buffer controlled_buffer_13
  buf buffer_12 (controlled_buffer_13_out, controlled_buffer_1_out);
  assign controlled_buffer_14_out = not_1_out ? sixteen_bit_adder_1_out_29 : 1'bz;  // Controlled_Buffer controlled_buffer_14
  buf buffer_13 (controlled_buffer_14_out, controlled_buffer_1_out);
  assign controlled_buffer_15_out = not_1_out ? sixteen_bit_adder_1_out_30 : 1'bz;  // Controlled_Buffer controlled_buffer_15
  buf buffer_14 (controlled_buffer_15_out, controlled_buffer_1_out);
  assign controlled_buffer_16_out = not_1_out ? sixteen_bit_adder_1_out_31 : 1'bz;  // Controlled_Buffer controlled_buffer_16
  buf buffer_15 (controlled_buffer_16_out, controlled_buffer_1_out);
  assign controlled_buffer_17_out = not_1_out ? sixteen_bit_adder_1_out_32 : 1'bz;  // Controlled_Buffer controlled_buffer_17
  buf buffer_16 (controlled_buffer_17_out, controlled_buffer_1_out);
  Clock clock_1 (.out(clock_1_out));
  register register_1 (
    .in_1(controlled_buffer_2_out), .in_7(controlled_buffer_8_out), .in_8(controlled_buffer_9_out),
    .in_9(clock_1_out), .in_10(in_1), .in_2(controlled_buffer_3_out), .in_3(controlled_buffer_4_out),
    .in_4(controlled_buffer_5_out), .in_5(controlled_buffer_6_out), .in_6(controlled_buffer_7_out),
    .out_16(register_1_out_16), .out_17(register_1_out_17), .out_18(register_1_out_18),
    .out_11(register_1_out_11), .out_12(register_1_out_12), .out_13(register_1_out_13),
    .out_14(register_1_out_14), .out_15(register_1_out_15));
  register register_2 (
    .in_1(controlled_buffer_10_out), .in_7(controlled_buffer_16_out), .in_8(controlled_buffer_17_out),
    .in_9(clock_1_out), .in_10(in_1), .in_2(controlled_buffer_11_out), .in_3(controlled_buffer_12_out),
    .in_4(controlled_buffer_13_out), .in_5(controlled_buffer_14_out), .in_6(controlled_buffer_15_out),
    .out_16(register_2_out_16), .out_17(register_2_out_17), .out_18(register_2_out_18),
    .out_11(register_2_out_11), .out_12(register_2_out_12), .out_13(register_2_out_13),
    .out_14(register_2_out_14), .out_15(register_2_out_15));
  not not_2 (not_2_out, clock_1_out);
  register register_3 (
    .in_1(register_1_out_11), .in_7(register_1_out_17), .in_8(register_1_out_18), .in_9(not_2_out),
    .in_10(in_1), .in_2(register_1_out_12), .in_3(register_1_out_13), .in_4(register_1_out_14),
    .in_5(register_1_out_15), .in_6(register_1_out_16), .out_16(out_8), .out_17(out_9), .out_18(out_10),
    .out_11(out_3), .out_12(out_4), .out_13(out_5), .out_14(out_6), .out_15(out_7));
  register register_4 (
    .in_1(register_2_out_11), .in_7(register_2_out_17), .in_8(register_2_out_18), .in_9(not_2_out),
    .in_10(in_1), .in_2(register_2_out_12), .in_3(register_2_out_13), .in_4(register_2_out_14),
    .in_5(register_2_out_15), .in_6(register_2_out_16), .out_16(out_16), .out_17(out_17), .out_18(out_18),
    .out_11(out_11), .out_12(out_12), .out_13(out_13), .out_14(out_14), .out_15(out_15));
endmodule

module D_type_flip_flop (
  input  in_1,
  input  in_2,
  output out_3
);

  wire and_1_out, and_2_out, not_1_out, not_3_out, or_1_out, or_2_out;

  not not_1 (not_1_out, in_1);
  and and_1 (and_1_out, not_1_out, in_2);
  and and_2 (and_2_out, in_2, in_1);
  or or_1 (or_1_out, and_1_out, not_3_out);
  not not_2 (out_3, or_1_out);
  or or_2 (or_2_out, out_3, and_2_out);
  not not_3 (not_3_out, or_2_out);
endmodule

module four_bit_ring_counter (
  input  in_1,
  input  in_2,
  output out_3,
  output out_4,
  output out_5,
  output out_6,
  output out_7,
  output out_8,
  output out_9
);

  wire controlled_buffer_1_out, controlled_buffer_8_out, d_type_flip_flop_1_out_3, d_type_flip_flop_2_out_3,
       d_type_flip_flop_3_out_3, d_type_flip_flop_4_out_3, d_type_flip_flop_5_out_3,
       d_type_flip_flop_6_out_3, d_type_flip_flop_7_out_3, d_type_flip_flop_8_out_3,
       d_type_flip_flop_9_out_3, d_type_flip_flop_10_out_3, d_type_flip_flop_11_out_3,
       d_type_flip_flop_12_out_3, d_type_flip_flop_13_out_3, not_1_out, not_2_out, not_3_out, not_4_out,
       not_5_out, not_6_out, not_7_out, not_8_out, not_9_out;

  D_type_flip_flop d_type_flip_flop_1 (.in_1(controlled_buffer_8_out), .in_2(in_2), .out_3(d_type_flip_flop_1_out_3));
  D_type_flip_flop d_type_flip_flop_2 (
    .in_1(d_type_flip_flop_1_out_3), .in_2(not_1_out), .out_3(d_type_flip_flop_2_out_3));
  not not_1 (not_1_out, in_2);
  assign controlled_buffer_1_out = in_1 ? 1'b0 : 1'bz;  // Controlled_Buffer controlled_buffer_1
  not not_2 (not_2_out, in_1);
  buf buffer_1 (out_3, controlled_buffer_1_out);
  assign out_3 = not_2_out ? d_type_flip_flop_2_out_3 : 1'bz;  // Controlled_Buffer controlled_buffer_2
  D_type_flip_flop d_type_flip_flop_3 (.in_1(out_3), .in_2(in_2), .out_3(d_type_flip_flop_3_out_3));
  D_type_flip_flop d_type_flip_flop_4 (
    .in_1(d_type_flip_flop_3_out_3), .in_2(not_3_out), .out_3(d_type_flip_flop_4_out_3));
  not not_3 (not_3_out, in_2);
  buf buffer_2 (out_4, controlled_buffer_1_out);
  assign out_4 = not_2_out ? d_type_flip_flop_4_out_3 : 1'bz;  // Controlled_Buffer controlled_buffer_3
  D_type_flip_flop d_type_flip_flop_5 (.in_1(out_4), .in_2(in_2), .out_3(d_type_flip_flop_5_out_3));
  D_type_flip_flop d_type_flip_flop_6 (
    .in_1(d_type_flip_flop_5_out_3), .in_2(not_4_out), .out_3(d_type_flip_flop_6_out_3));
  not not_4 (not_4_out, in_2);
  assign out_5 = not_2_out ? d_type_flip_flop_6_out_3 : 1'bz;  // Controlled_Buffer controlled_buffer_4
  buf buffer_3 (out_5, controlled_buffer_1_out);
  D_type_flip_flop d_type_flip_flop_7 (.in_1(out_5), .in_2(in_2), .out_3(d_type_flip_flop_7_out_3));
  not not_5 (not_5_out, in_2);
  assign out_6 = not_2_out ? d_type_flip_flop_8_out_3 : 1'bz;  // Controlled_Buffer controlled_buffer_5
  D_type_flip_flop d_type_flip_flop_8 (
    .in_1(d_type_flip_flop_7_out_3), .in_2(not_5_out), .out_3(d_type_flip_flop_8_out_3));
  buf buffer_4 (out_6, controlled_buffer_1_out);
  D_type_flip_flop d_type_flip_flop_9 (.in_1(out_6), .in_2(in_2), .out_3(d_type_flip_flop_9_out_3));
  not not_6 (not_6_out, in_2);
  assign out_7 = not_2_out ? d_type_flip_flop_10_out_3 : 1'bz;  // Controlled_Buffer controlled_buffer_6
  D_type_flip_flop d_type_flip_flop_10 (
    .in_1(d_type_flip_flop_9_out_3), .in_2(not_6_out), .out_3(d_type_flip_flop_10_out_3));
  buf buffer_5 (out_7, controlled_buffer_1_out);
  D_type_flip_flop d_type_flip_flop_11 (.in_1(out_7), .in_2(in_2), .out_3(d_type_flip_flop_11_out_3));
  not not_7 (not_7_out, in_2);
  D_type_flip_flop d_type_flip_flop_12 (
    .in_1(d_type_flip_flop_11_out_3), .in_2(not_7_out), .out_3(d_type_flip_flop_12_out_3));
  buf buffer_6 (out_8, controlled_buffer_1_out);
  assign out_8 = not_2_out ? d_type_flip_flop_12_out_3 : 1'bz;  // Controlled_Buffer controlled_buffer_7
  not not_8 (not_8_out, not_2_out);
  assign controlled_buffer_8_out = not_8_out ? 1'b1 : 1'bz;  // Controlled_Buffer controlled_buffer_8
  assign controlled_buffer_8_out = not_2_out ? out_9 : 1'bz;  // Controlled_Buffer controlled_buffer_9
  D_type_flip_flop d_type_flip_flop_13 (.in_1(out_8), .in_2(in_2), .out_3(d_type_flip_flop_13_out_3));
  D_type_flip_flop d_type_flip_flop_14 (.in_1(d_type_flip_flop_13_out_3), .in_2(not_9_out), .out_3(out_9));
  not not_9 (not_9_out, in_2);
endmodule

module register (
  input  in_1,
  input  in_2,
  input  in_3,
  input  in_4,
  input  in_5,
  input  in_6,
  input  in_7,
  input  in_8,
  input  in_9,
  input  in_10,
  output out_11,
  output out_12,
  output out_13,
  output out_14,
  output out_15,
  output out_16,
  output out_17,
  output out_18
);

  wire and_1_out, and_2_out, and_3_out, and_4_out, and_5_out, and_6_out, and_7_out, and_8_out, xor_1_out,
       xor_2_out, xor_3_out, xor_4_out, xor_5_out, xor_6_out, xor_7_out, xor_8_out;

  and and_1 (and_1_out, in_1, in_10);
  xor xor_1 (xor_1_out, in_1, and_1_out);
  D_type_flip_flop d_type_flip_flop_1 (.in_1(xor_1_out), .in_2(in_9), .out_3(out_11));
  xor xor_2 (xor_2_out, in_2, and_2_out);
  and and_2 (and_2_out, in_2, in_10);
  D_type_flip_flop d_type_flip_flop_2 (.in_1(xor_2_out), .in_2(in_9), .out_3(out_12));
  xor xor_3 (xor_3_out, in_3, and_3_out);
  and and_3 (and_3_out, in_3, in_10);
  D_type_flip_flop d_type_flip_flop_3 (.in_1(xor_3_out), .in_2(in_9), .out_3(out_13));
  xor xor_4 (xor_4_out, in_4, and_4_out);
  and and_4 (and_4_out, in_4, in_10);
  D_type_flip_flop d_type_flip_flop_4 (.in_1(xor_4_out), .in_2(in_9), .out_3(out_14));
  xor xor_5 (xor_5_out, in_5, and_5_out);
  and and_5 (and_5_out, in_5, in_10);
  D_type_flip_flop d_type_flip_flop_5 (.in_1(xor_5_out), .in_2(in_9), .out_3(out_15));
  and and_6 (and_6_out, in_6, in_10);
  xor xor_6 (xor_6_out, in_6, and_6_out);
  D_type_flip_flop d_type_flip_flop_6 (.in_1(xor_6_out), .in_2(in_9), .out_3(out_16));
  and and_7 (and_7_out, in_7, in_10);
  xor xor_7 (xor_7_out, in_7, and_7_out);
  D_type_flip_flop d_type_flip_flop_7 (.in_1(xor_7_out), .in_2(in_9), .out_3(out_17));
  and and_8 (and_8_out, in_8, in_10);
  xor xor_8 (xor_8_out, in_8, and_8_out);
  D_type_flip_flop d_type_flip_flop_8 (.in_1(xor_8_out), .in_2(in_9), .out_3(out_18));
endmodule

module PC (
  input  in_1,
  input  in_2,
  output out_3,
  output out_4,
  output out_5,
  output out_6,
  output out_7,
  output out_8,
  output out_9,
  output out_10,
  output out_11,
  output out_12,
  output out_13,
  output out_14,
  output out_15,
  output out_16,
  output out_17,
  output out_18,
  output out_19,
  output out_20,
  output out_21,
  output out_22,
  output out_23,
  output out_24,
  output out_25
);

  wire and_1_out, controlled_buffer_1_out, not_1_out, or_1_out;

  and and_1 (and_1_out, in_2, controlled_buffer_1_out);
  four_bit_ring_counter four_bit_ring_counter_1 (
    .in_2(in_2), .in_1(in_1), .out_8(out_20), .out_9(out_21), .out_3(out_22), .out_4(out_23), .out_5(out_24),
    .out_6(out_25), .out_7(out_19));
  Counter counter_1 (
    .in_2(and_1_out), .in_1(in_1), .out_11(out_11), .out_12(out_12), .out_13(out_13), .out_14(out_14),
    .out_15(out_15), .out_16(out_16), .out_17(out_17), .out_18(out_18), .out_3(out_3), .out_4(out_4),
    .out_5(out_5), .out_6(out_6), .out_7(out_7), .out_8(out_8), .out_9(out_9), .out_10(out_10));
  or or_1 (or_1_out, out_22, out_23, out_24, out_25);
  assign controlled_buffer_1_out = not_1_out ? or_1_out : 1'bz;  // Controlled_Buffer controlled_buffer_1
  not not_1 (not_1_out, in_1);
  assign controlled_buffer_1_out = in_1 ? in_1 : 1'bz;  // Controlled_Buffer controlled_buffer_2
endmodule

module Demux_1_2 (
  input  in_1,
  input  in_2,
  output out_3,
  output out_4
);

  wire not_1_out;

  not not_1 (not_1_out, in_2);
  and and_1 (out_3, not_1_out, in_1);
  and and_2 (out_4, in_1, in_2);
endmodule

module Demux_1_16 (
  input  in_1,
  input  in_2,
  input  in_3,
  input  in_4,
  input  in_5,
  output out_6,
  output out_7,
  output out_8,
  output out_9,
  output out_10,
  output out_11,
  output out_12,
  output out_13,
  output out_14,
  output out_15,
  output out_16,
  output out_17,
  output out_18,
  output out_19,
  output out_20,
  output out_21
);

  wire demux_1_2_1_out_3, demux_1_2_1_out_4, demux_1_2_2_out_3, demux_1_2_2_out_4, demux_1_2_3_out_3,
       demux_1_2_3_out_4, demux_1_2_4_out_3, demux_1_2_4_out_4, demux_1_2_5_out_3, demux_1_2_5_out_4,
       demux_1_2_6_out_3, demux_1_2_6_out_4, demux_1_2_7_out_3, demux_1_2_7_out_4;

  Demux_1_2 demux_1_2_1 (.in_1(in_5), .in_2(in_4), .out_3(demux_1_2_1_out_3), .out_4(demux_1_2_1_out_4));
  Demux_1_2 demux_1_2_2 (.in_1(demux_1_2_1_out_3), .in_2(in_3), .out_3(demux_1_2_2_out_3), .out_4(demux_1_2_2_out_4));
  Demux_1_2 demux_1_2_3 (.in_1(demux_1_2_1_out_4), .in_2(in_3), .out_3(demux_1_2_3_out_3), .out_4(demux_1_2_3_out_4));
  Demux_1_2 demux_1_2_4 (.in_1(demux_1_2_2_out_3), .in_2(in_2), .out_3(demux_1_2_4_out_3), .out_4(demux_1_2_4_out_4));
  Demux_1_2 demux_1_2_5 (.in_1(demux_1_2_2_out_4), .in_2(in_2), .out_3(demux_1_2_5_out_3), .out_4(demux_1_2_5_out_4));
  Demux_1_2 demux_1_2_6 (.in_1(demux_1_2_3_out_3), .in_2(in_2), .out_3(demux_1_2_6_out_3), .out_4(demux_1_2_6_out_4));
  Demux_1_2 demux_1_2_7 (.in_1(demux_1_2_3_out_4), .in_2(in_2), .out_3(demux_1_2_7_out_3), .out_4(demux_1_2_7_out_4));
  Demux_1_2 demux_1_2_8 (.in_1(demux_1_2_4_out_3), .in_2(in_1), .out_3(out_6), .out_4(out_7));
  Demux_1_2 demux_1_2_9 (.in_1(demux_1_2_4_out_4), .in_2(in_1), .out_3(out_8), .out_4(out_9));
  Demux_1_2 demux_1_2_10 (.in_1(demux_1_2_5_out_3), .in_2(in_1), .out_3(out_10), .out_4(out_11));
  Demux_1_2 demux_1_2_11 (.in_1(demux_1_2_5_out_4), .in_2(in_1), .out_3(out_12), .out_4(out_13));
  Demux_1_2 demux_1_2_12 (.in_1(demux_1_2_6_out_3), .in_2(in_1), .out_3(out_14), .out_4(out_15));
  Demux_1_2 demux_1_2_13 (.in_1(demux_1_2_6_out_4), .in_2(in_1), .out_3(out_16), .out_4(out_17));
  Demux_1_2 demux_1_2_14 (.in_1(demux_1_2_7_out_3), .in_2(in_1), .out_3(out_18), .out_4(out_19));
  Demux_1_2 demux_1_2_15 (.in_1(demux_1_2_7_out_4), .in_2(in_1), .out_3(out_20), .out_4(out_21));
endmodule

module demux_1_64 (
  input  in_1,
  input  in_2,
  input  in_3,
  input  in_4,
  input  in_5,
  input  in_6,
  input  in_7,
  output out_8,
  output out_9,
  output out_10,
  output out_11,
  output out_12,
  output out_13,
  output out_14,
  output out_15,
  output out_16,
  output out_17,
  output out_18,
  output out_19,
  output out_20,
  output out_21,
  output out_22,
  output out_23,
  output out_24,
  output out_25,
  output out_26,
  output out_27,
  output out_28,
  output out_29,
  output out_30,
  output out_31,
  output out_32,
  output out_33,
  output out_34,
  output out_35,
  output out_36,
  output out_37,
  output out_38,
  output out_39,
  output out_40,
  output out_41,
  output out_42,
  output out_43,
  output out_44,
  output out_45,
  output out_46,
  output out_47,
  output out_48,
  output out_49,
  output out_50,
  output out_51,
  output out_52,
  output out_53,
  output out_54,
  output out_55,
  output out_56,
  output out_57,
  output out_58,
  output out_59,
  output out_60,
  output out_61,
  output out_62,
  output out_63,
  output out_64,
  output out_65,
  output out_66,
  output out_67,
  output out_68,
  output out_69,
  output out_70,
  output out_71,
  output out_72
);

  wire demux_1_16_1_out_6, demux_1_16_1_out_7, demux_1_16_1_out_8, demux_1_16_1_out_9, undriven;

  Demux_1_16 demux_1_16_1 (
    .in_3(undriven), .in_2(in_6), .in_1(in_7), .in_4(undriven), .in_5(in_5), .out_7(demux_1_16_1_out_7),
    .out_8(demux_1_16_1_out_8), .out_9(demux_1_16_1_out_9), .out_10(out_44), .out_11(out_44),
    .out_12(out_44), .out_13(out_44), .out_14(out_44), .out_15(out_44), .out_16(out_44), .out_17(out_44),
    .out_18(out_44), .out_19(out_44), .out_20(out_44), .out_21(out_44), .out_6(demux_1_16_1_out_6));
  Demux_1_16 demux_1_16_2 (
    .in_3(in_2), .in_2(in_3), .in_1(in_4), .in_4(in_1), .in_5(demux_1_16_1_out_6), .out_7(out_9),
    .out_8(out_10), .out_9(out_11), .out_10(out_12), .out_11(out_13), .out_12(out_14), .out_13(out_15),
    .out_14(out_16), .out_15(out_17), .out_16(out_18), .out_17(out_19), .out_18(out_20), .out_19(out_21),
    .out_20(out_22), .out_21(out_23), .out_6(out_8));
  Demux_1_16 demux_1_16_3 (
    .in_3(in_2), .in_2(in_3), .in_1(in_4), .in_4(in_1), .in_5(demux_1_16_1_out_7), .out_7(out_25),
    .out_8(out_26), .out_9(out_27), .out_10(out_28), .out_11(out_29), .out_12(out_30), .out_13(out_31),
    .out_14(out_32), .out_15(out_33), .out_16(out_34), .out_17(out_35), .out_18(out_36), .out_19(out_37),
    .out_20(out_38), .out_21(out_39), .out_6(out_24));
  Demux_1_16 demux_1_16_4 (
    .in_3(in_2), .in_2(in_3), .in_1(in_4), .in_4(in_1), .in_5(demux_1_16_1_out_8), .out_7(out_41),
    .out_8(out_42), .out_9(out_43), .out_10(out_45), .out_11(out_46), .out_12(out_47), .out_13(out_48),
    .out_14(out_49), .out_15(out_50), .out_16(out_51), .out_17(out_52), .out_18(out_53), .out_19(out_54),
    .out_20(out_55), .out_21(out_56), .out_6(out_40));
  Demux_1_16 demux_1_16_5 (
    .in_3(in_2), .in_2(in_3), .in_1(in_4), .in_4(in_1), .in_5(demux_1_16_1_out_9), .out_7(out_58),
    .out_8(out_59), .out_9(out_60), .out_10(out_61), .out_11(out_62), .out_12(out_63), .out_13(out_64),
    .out_14(out_65), .out_15(out_66), .out_16(out_67), .out_17(out_68), .out_18(out_69), .out_19(out_70),
    .out_20(out_71), .out_21(out_72), .out_6(out_57));
endmodule

module instruction_register (
  input  in_1,
  input  in_2,
  input  in_3,
  input  in_4,
  input  in_5,
  input  in_6,
  input  in_7,
  input  in_8,
  input  in_9,
  input  in_10,
  input  in_11,
  input  in_12,
  input  in_13,
  output out_14,
  output out_15,
  output out_16,
  output out_17,
  output out_18,
  output out_19,
  output out_20,
  output out_21,
  output out_22,
  output out_23,
  output out_24,
  output out_25,
  output out_26,
  output out_27,
  output out_28,
  output out_29,
  output out_30,
  output out_31,
  output out_32,
  output out_33,
  output out_34,
  output out_35,
  output out_36,
  output out_37,
  output out_38,
  output out_39,
  output out_40,
  output out_41,
  output out_42,
  output out_43,
  output out_44,
  output out_45
);

  wire controlled_buffer_1_out, controlled_buffer_3_out, controlled_buffer_5_out, controlled_buffer_7_out,
       not_1_out, not_2_out, not_3_out, not_4_out;

  register register_1 (
    .in_1(in_2), .in_7(in_8), .in_8(in_9), .in_9(controlled_buffer_1_out), .in_10(in_1), .in_2(in_3),
    .in_3(in_4), .in_4(in_5), .in_5(in_6), .in_6(in_7), .out_16(out_19), .out_17(out_20), .out_18(out_21),
    .out_11(out_14), .out_12(out_15), .out_13(out_16), .out_14(out_17), .out_15(out_18));
  assign controlled_buffer_1_out = in_1 ? in_1 : 1'bz;  // Controlled_Buffer controlled_buffer_1
  assign controlled_buffer_1_out = not_1_out ? in_10 : 1'bz;  // Controlled_Buffer controlled_buffer_2
  not not_1 (not_1_out, in_1);
  register register_2 (
    .in_1(in_2), .in_7(in_8), .in_8(in_9), .in_9(controlled_buffer_3_out), .in_10(in_1), .in_2(in_3),
    .in_3(in_4), .in_4(in_5), .in_5(in_6), .in_6(in_7), .out_16(out_27), .out_17(out_28), .out_18(out_29),
    .out_11(out_22), .out_12(out_23), .out_13(out_24), .out_14(out_25), .out_15(out_26));
  assign controlled_buffer_3_out = in_1 ? in_1 : 1'bz;  // Controlled_Buffer controlled_buffer_3
  assign controlled_buffer_3_out = not_2_out ? in_11 : 1'bz;  // Controlled_Buffer controlled_buffer_4
  not not_2 (not_2_out, in_1);
  register register_3 (
    .in_1(in_2), .in_7(in_8), .in_8(in_9), .in_9(controlled_buffer_5_out), .in_10(in_1), .in_2(in_3),
    .in_3(in_4), .in_4(in_5), .in_5(in_6), .in_6(in_7), .out_16(out_35), .out_17(out_36), .out_18(out_37),
    .out_11(out_30), .out_12(out_31), .out_13(out_32), .out_14(out_33), .out_15(out_34));
  assign controlled_buffer_5_out = in_1 ? in_1 : 1'bz;  // Controlled_Buffer controlled_buffer_5
  assign controlled_buffer_5_out = not_3_out ? in_12 : 1'bz;  // Controlled_Buffer controlled_buffer_6
  not not_3 (not_3_out, in_1);
  register register_4 (
    .in_1(in_2), .in_7(in_8), .in_8(in_9), .in_9(controlled_buffer_7_out), .in_10(in_1), .in_2(in_3),
    .in_3(in_4), .in_4(in_5), .in_5(in_6), .in_6(in_7), .out_16(out_43), .out_17(out_44), .out_18(out_45),
    .out_11(out_38), .out_12(out_39), .out_13(out_40), .out_14(out_41), .out_15(out_42));
  assign controlled_buffer_7_out = in_1 ? in_1 : 1'bz;  // Controlled_Buffer controlled_buffer_7
  assign controlled_buffer_7_out = not_4_out ? in_13 : 1'bz;  // Controlled_Buffer controlled_buffer_8
  not not_4 (not_4_out, in_1);
endmodule

module sixteen_bit_adder (
  input  in_1,
  input  in_2,
  input  in_3,
  input  in_4,
  input  in_5,
  input  in_6,
  input  in_7,
  input  in_8,
  input  in_9,
  input  in_10,
  input  in_11,
  input  in_12,
  input  in_13,
  input  in_14,
  input  in_15,
  input  in_16,
  input  in_17,
  output out_18,
  output out_19,
  output out_20,
  output out_21,
  output out_22,
  output out_23,
  output out_24,
  output out_25,
  output out_26,
  output out_27,
  output out_28,
  output out_29,
  output out_30,
  output out_31,
  output out_32,
  output out_33
);

  wire full_adder_1_out_5, full_adder_2_out_5, full_adder_3_out_5, full_adder_4_out_5, full_adder_5_out_5,
       full_adder_6_out_5, full_adder_7_out_5, full_adder_8_out_5, full_adder_9_out_5, full_adder_10_out_5,
       full_adder_11_out_5, full_adder_12_out_5, full_adder_13_out_5, full_adder_14_out_5, half_adder_1_out_4;

  half_adder half_adder_1 (.in_1(in_16), .in_2(in_17), .out_4(half_adder_1_out_4), .out_3(out_33));
  full_adder full_adder_1 (
    .in_3(half_adder_1_out_4), .in_1(in_1), .out_4(out_18), .out_5(full_adder_1_out_5));  // open: in_2
  full_adder full_adder_2 (
    .in_3(full_adder_1_out_5), .in_2(1'b0), .in_1(in_2), .out_4(out_19), .out_5(full_adder_2_out_5));
  full_adder full_adder_3 (
    .in_3(full_adder_2_out_5), .in_2(1'b0), .in_1(in_3), .out_4(out_20), .out_5(full_adder_3_out_5));
  full_adder full_adder_4 (
    .in_3(full_adder_3_out_5), .in_2(1'b0), .in_1(in_4), .out_4(out_21), .out_5(full_adder_4_out_5));
  full_adder full_adder_5 (
    .in_3(full_adder_4_out_5), .in_2(1'b0), .in_1(in_5), .out_4(out_22), .out_5(full_adder_5_out_5));
  full_adder full_adder_6 (
    .in_3(full_adder_5_out_5), .in_2(1'b0), .in_1(in_6), .out_4(out_23), .out_5(full_adder_6_out_5));
  full_adder full_adder_7 (
    .in_3(full_adder_6_out_5), .in_2(1'b0), .in_1(in_7), .out_4(out_24), .out_5(full_adder_7_out_5));
  full_adder full_adder_8 (
    .in_3(full_adder_7_out_5), .in_2(1'b0), .in_1(in_8), .out_4(out_25), .out_5(full_adder_8_out_5));
  full_adder full_adder_9 (
    .in_3(full_adder_8_out_5), .in_2(1'b0), .in_1(in_9), .out_4(out_26), .out_5(full_adder_9_out_5));
  full_adder full_adder_10 (
    .in_3(full_adder_9_out_5), .in_2(1'b0), .in_1(in_10), .out_4(out_27), .out_5(full_adder_10_out_5));
  full_adder full_adder_11 (
    .in_3(full_adder_10_out_5), .in_2(1'b0), .in_1(in_11), .out_4(out_28), .out_5(full_adder_11_out_5));
  full_adder full_adder_12 (
    .in_3(full_adder_11_out_5), .in_2(1'b0), .in_1(in_12), .out_4(out_29), .out_5(full_adder_12_out_5));
  full_adder full_adder_13 (
    .in_3(full_adder_12_out_5), .in_2(1'b0), .in_1(in_13), .out_4(out_30), .out_5(full_adder_13_out_5));
  full_adder full_adder_14 (
    .in_3(full_adder_13_out_5), .in_2(1'b0), .in_1(in_14), .out_4(out_31), .out_5(full_adder_14_out_5));
  full_adder full_adder_15 (.in_3(full_adder_14_out_5), .in_2(1'b0), .in_1(in_15), .out_4(out_32));  // open: out_5
endmodule

module sixtyfour_byte_reg (
);

  wire demux_1_16_1_out_6, demux_1_16_1_out_7, demux_1_16_1_out_8, demux_1_16_1_out_9, demux_1_16_1_out_10,
       demux_1_16_1_out_11, demux_1_16_1_out_12, demux_1_16_1_out_13, demux_1_16_1_out_14,
       demux_1_16_1_out_15, demux_1_16_1_out_16, demux_1_16_1_out_17, demux_1_16_1_out_18,
       demux_1_16_1_out_19, demux_1_16_1_out_20, demux_1_16_1_out_21, demux_1_16_2_out_6, demux_1_16_2_out_7,
       demux_1_16_2_out_8, demux_1_16_2_out_9, demux_1_16_2_out_10, demux_1_16_2_out_11, demux_1_16_2_out_12,
       demux_1_16_2_out_13, demux_1_16_2_out_14, demux_1_16_2_out_15, demux_1_16_2_out_16,
       demux_1_16_2_out_17, demux_1_16_2_out_18, demux_1_16_2_out_19, demux_1_16_2_out_20,
       demux_1_16_2_out_21, sixteen_byte_reg_1_out_19, sixteen_byte_reg_1_out_22, sixteen_byte_reg_1_out_26,
       undriven, undriven_2, undriven_3;

  Demux_1_16 demux_1_16_1 (
    .out_7(demux_1_16_1_out_7), .out_8(demux_1_16_1_out_8), .out_9(demux_1_16_1_out_9),
    .out_10(demux_1_16_1_out_10), .out_11(demux_1_16_1_out_11), .out_12(demux_1_16_1_out_12),
    .out_13(demux_1_16_1_out_13), .out_14(demux_1_16_1_out_14), .out_15(demux_1_16_1_out_15),
    .out_16(demux_1_16_1_out_16), .out_17(demux_1_16_1_out_17), .out_18(demux_1_16_1_out_18),
    .out_19(demux_1_16_1_out_19), .out_20(demux_1_16_1_out_20), .out_21(demux_1_16_1_out_21),
    .out_6(demux_1_16_1_out_6));  // open: in_3, in_2, in_1, in_4, in_5
  Demux_1_16 demux_1_16_2 (
    .out_7(demux_1_16_2_out_7), .out_8(demux_1_16_2_out_8), .out_9(demux_1_16_2_out_9),
    .out_10(demux_1_16_2_out_10), .out_11(demux_1_16_2_out_11), .out_12(demux_1_16_2_out_12),
    .out_13(demux_1_16_2_out_13), .out_14(demux_1_16_2_out_14), .out_15(demux_1_16_2_out_15),
    .out_16(demux_1_16_2_out_16), .out_17(demux_1_16_2_out_17), .out_18(demux_1_16_2_out_18),
    .out_19(demux_1_16_2_out_19), .out_20(demux_1_16_2_out_20), .out_21(demux_1_16_2_out_21),
    .out_6(demux_1_16_2_out_6));  // open: in_3, in_2, in_1, in_4, in_5
  sixteen_byte_reg sixteen_byte_reg_1 (
    .in_15(demux_1_16_2_out_6), .in_16(demux_1_16_2_out_7), .in_17(demux_1_16_2_out_8),
    .in_18(demux_1_16_2_out_9), .in_14(undriven_3), .in_9(demux_1_16_1_out_9), .in_10(demux_1_16_1_out_8),
    .in_11(demux_1_16_1_out_7), .in_12(demux_1_16_1_out_6), .in_13(undriven_3), .in_1(undriven_3),
    .in_2(undriven_3), .in_3(undriven_3), .in_4(undriven_3), .in_5(undriven_3), .in_6(undriven),
    .in_7(undriven_3), .in_8(undriven_2), .out_22(sixteen_byte_reg_1_out_22),
    .out_23(sixteen_byte_reg_1_out_22), .out_24(sixteen_byte_reg_1_out_22),
    .out_25(sixteen_byte_reg_1_out_22), .out_26(sixteen_byte_reg_1_out_26),
    .out_19(sixteen_byte_reg_1_out_19), .out_20(sixteen_byte_reg_1_out_22), .out_21(sixteen_byte_reg_1_out_22));
  sixteen_byte_reg sixteen_byte_reg_2 (
    .in_15(demux_1_16_2_out_10), .in_16(demux_1_16_2_out_11), .in_17(demux_1_16_2_out_12),
    .in_18(demux_1_16_2_out_13), .in_14(undriven_3), .in_9(demux_1_16_1_out_13), .in_10(demux_1_16_1_out_12),
    .in_11(demux_1_16_1_out_11), .in_12(demux_1_16_1_out_10), .in_13(undriven_3), .in_1(undriven_3),
    .in_2(undriven_3), .in_3(undriven_3), .in_4(undriven_3), .in_5(undriven_3), .in_6(undriven),
    .in_7(undriven_3), .in_8(undriven_2), .out_22(sixteen_byte_reg_1_out_22),
    .out_23(sixteen_byte_reg_1_out_22), .out_24(sixteen_byte_reg_1_out_22),
    .out_25(sixteen_byte_reg_1_out_22), .out_26(sixteen_byte_reg_1_out_26),
    .out_19(sixteen_byte_reg_1_out_19), .out_20(sixteen_byte_reg_1_out_22), .out_21(sixteen_byte_reg_1_out_22));
  sixteen_byte_reg sixteen_byte_reg_3 (
    .in_15(demux_1_16_2_out_14), .in_16(demux_1_16_2_out_15), .in_17(demux_1_16_2_out_16),
    .in_18(demux_1_16_2_out_17), .in_14(undriven_3), .in_9(demux_1_16_1_out_17), .in_10(demux_1_16_1_out_16),
    .in_11(demux_1_16_1_out_15), .in_12(demux_1_16_1_out_14), .in_13(undriven_3), .in_1(undriven_3),
    .in_2(undriven_3), .in_3(undriven_3), .in_4(undriven_3), .in_5(undriven_3), .in_6(undriven),
    .in_7(undriven_3), .in_8(undriven_2), .out_22(sixteen_byte_reg_1_out_22),
    .out_23(sixteen_byte_reg_1_out_22), .out_24(sixteen_byte_reg_1_out_22),
    .out_25(sixteen_byte_reg_1_out_22), .out_26(sixteen_byte_reg_1_out_26),
    .out_19(sixteen_byte_reg_1_out_19), .out_20(sixteen_byte_reg_1_out_22), .out_21(sixteen_byte_reg_1_out_22));
  sixteen_byte_reg sixteen_byte_reg_4 (
    .in_15(demux_1_16_2_out_18), .in_16(demux_1_16_2_out_19), .in_17(demux_1_16_2_out_20),
    .in_18(demux_1_16_2_out_21), .in_14(undriven_3), .in_9(demux_1_16_1_out_21), .in_10(demux_1_16_1_out_20),
    .in_11(demux_1_16_1_out_19), .in_12(demux_1_16_1_out_18), .in_13(undriven_3), .in_1(undriven_3),
    .in_2(undriven_3), .in_3(undriven_3), .in_4(undriven_3), .in_5(undriven_3), .in_6(undriven),
    .in_7(undriven_3), .in_8(undriven_2));  // open: out_22, out_23, out_24, out_25, out_26, out_19, out_20, out_21
endmodule

module sixteen_byte_reg (
  input  in_1,
  input  in_2,
  input  in_3,
  input  in_4,
  input  in_5,
  input  in_6,
  input  in_7,
  input  in_8,
  input  in_9,
  input  in_10,
  input  in_11,
  input  in_12,
  input  in_13,
  input  in_14,
  input  in_15,
  input  in_16,
  input  in_17,
  input  in_18,
  output out_19,
  output out_20,
  output out_21,
  output out_22,
  output out_23,
  output out_24,
  output out_25,
  output out_26
);

  wire demux_1_16_1_out_6, demux_1_16_1_out_7, demux_1_16_1_out_8, demux_1_16_1_out_9, demux_1_16_1_out_10,
       demux_1_16_1_out_11, demux_1_16_1_out_12, demux_1_16_1_out_13, demux_1_16_1_out_14,
       demux_1_16_1_out_15, demux_1_16_1_out_16, demux_1_16_1_out_17, demux_1_16_1_out_18,
       demux_1_16_1_out_19, demux_1_16_1_out_20, demux_1_16_1_out_21, demux_1_16_2_out_6, demux_1_16_2_out_7,
       demux_1_16_2_out_8, demux_1_16_2_out_9, demux_1_16_2_out_10, demux_1_16_2_out_11, demux_1_16_2_out_12,
       demux_1_16_2_out_13, demux_1_16_2_out_14, demux_1_16_2_out_15, demux_1_16_2_out_16,
       demux_1_16_2_out_17, demux_1_16_2_out_18, demux_1_16_2_out_19, demux_1_16_2_out_20,
       demux_1_16_2_out_21, register_12_out_18, register_13_out_11, register_13_out_12, register_13_out_13,
       register_13_out_14, register_13_out_15, register_13_out_16, register_13_out_17, register_13_out_18,
       register_16_out_18;

  Demux_1_16 demux_1_16_1 (
    .in_3(in_16), .in_2(in_17), .in_1(in_18), .in_4(in_15), .in_5(in_14), .out_7(demux_1_16_1_out_7),
    .out_8(demux_1_16_1_out_8), .out_9(demux_1_16_1_out_9), .out_10(demux_1_16_1_out_10),
    .out_11(demux_1_16_1_out_11), .out_12(demux_1_16_1_out_12), .out_13(demux_1_16_1_out_13),
    .out_14(demux_1_16_1_out_14), .out_15(demux_1_16_1_out_15), .out_16(demux_1_16_1_out_16),
    .out_17(demux_1_16_1_out_17), .out_18(demux_1_16_1_out_18), .out_19(demux_1_16_1_out_19),
    .out_20(demux_1_16_1_out_20), .out_21(demux_1_16_1_out_21), .out_6(demux_1_16_1_out_6));
  register register_1 (
    .in_1(in_8), .in_7(in_2), .in_8(in_1), .in_9(demux_1_16_1_out_6), .in_10(demux_1_16_2_out_6),
    .in_2(in_7), .in_3(in_6), .in_4(in_5), .in_5(in_4), .in_6(in_3), .out_16(out_19), .out_17(out_19),
    .out_18(out_19), .out_11(out_19), .out_12(out_19), .out_13(out_19), .out_14(out_19), .out_15(out_19));
  register register_2 (
    .in_1(in_8), .in_7(in_2), .in_8(in_1), .in_9(demux_1_16_1_out_10), .in_10(demux_1_16_2_out_10),
    .in_2(in_7), .in_3(in_6), .in_4(in_5), .in_5(in_4), .in_6(in_3), .out_16(out_19), .out_17(out_19),
    .out_18(out_19), .out_11(out_19), .out_12(out_19), .out_13(out_19), .out_14(out_19), .out_15(out_19));
  register register_3 (
    .in_1(in_8), .in_7(in_2), .in_8(in_1), .in_9(demux_1_16_1_out_14), .in_10(demux_1_16_2_out_14),
    .in_2(in_7), .in_3(in_6), .in_4(in_5), .in_5(in_4), .in_6(in_3), .out_16(out_19), .out_17(out_19),
    .out_18(out_19), .out_11(out_19), .out_12(out_19), .out_13(out_19), .out_14(out_19), .out_15(out_19));
  register register_4 (
    .in_1(in_8), .in_7(in_2), .in_8(in_1), .in_9(demux_1_16_1_out_18), .in_10(demux_1_16_2_out_18),
    .in_2(in_7), .in_3(in_6), .in_4(in_5), .in_5(in_4), .in_6(in_3), .out_16(out_19), .out_17(out_19),
    .out_18(out_19), .out_11(out_19), .out_12(out_19), .out_13(out_19), .out_14(out_19), .out_15(out_19));
  register register_5 (
    .in_1(in_8), .in_7(in_2), .in_8(in_1), .in_9(demux_1_16_1_out_7), .in_10(demux_1_16_2_out_7),
    .in_2(in_7), .in_3(in_6), .in_4(in_5), .in_5(in_4), .in_6(in_3), .out_16(out_19), .out_17(out_19),
    .out_18(out_19), .out_11(out_19), .out_12(out_19), .out_13(out_19), .out_14(out_19), .out_15(out_19));
  register register_6 (
    .in_1(in_8), .in_7(in_2), .in_8(in_1), .in_9(demux_1_16_1_out_11), .in_10(demux_1_16_2_out_11),
    .in_2(in_7), .in_3(in_6), .in_4(in_5), .in_5(in_4), .in_6(in_3), .out_16(out_19), .out_17(out_19),
    .out_18(out_19), .out_11(out_19), .out_12(out_19), .out_13(out_19), .out_14(out_19), .out_15(out_19));
  register register_7 (
    .in_1(in_8), .in_7(in_2), .in_8(in_1), .in_9(demux_1_16_1_out_15), .in_10(demux_1_16_2_out_15),
    .in_2(in_7), .in_3(in_6), .in_4(in_5), .in_5(in_4), .in_6(in_3), .out_16(out_19), .out_17(out_19),
    .out_18(out_19), .out_11(out_19), .out_12(out_19), .out_13(out_19), .out_14(out_19), .out_15(out_19));
  register register_8 (
    .in_1(in_8), .in_7(in_2), .in_8(in_1), .in_9(demux_1_16_1_out_19), .in_10(demux_1_16_2_out_19),
    .in_2(in_7), .in_3(in_6), .in_4(in_5), .in_5(in_4), .in_6(in_3), .out_16(out_19), .out_17(out_19),
    .out_18(out_19), .out_11(out_19), .out_12(out_19), .out_13(out_19), .out_14(out_19), .out_15(out_19));
  register register_9 (
    .in_1(in_8), .in_7(in_2), .in_8(in_1), .in_9(demux_1_16_1_out_8), .in_10(demux_1_16_2_out_8),
    .in_2(in_7), .in_3(in_6), .in_4(in_5), .in_5(in_4), .in_6(in_3), .out_16(out_19), .out_17(out_19),
    .out_18(out_19), .out_11(out_19), .out_12(out_19), .out_13(out_19), .out_14(out_19), .out_15(out_19));
  register register_10 (
    .in_1(in_8), .in_7(in_2), .in_8(in_1), .in_9(demux_1_16_1_out_12), .in_10(demux_1_16_2_out_12),
    .in_2(in_7), .in_3(in_6), .in_4(in_5), .in_5(in_4), .in_6(in_3), .out_16(out_19), .out_17(out_19),
    .out_18(out_19), .out_11(out_19), .out_12(out_19), .out_13(out_19), .out_14(out_19), .out_15(out_19));
  register register_11 (
    .in_1(in_8), .in_7(in_2), .in_8(in_1), .in_9(demux_1_16_1_out_16), .in_10(demux_1_16_2_out_16),
    .in_2(in_7), .in_3(in_6), .in_4(in_5), .in_5(in_4), .in_6(in_3), .out_16(out_19), .out_17(out_19),
    .out_18(out_19), .out_11(out_19), .out_12(out_19), .out_13(out_19), .out_14(out_19), .out_15(out_19));
  register register_12 (
    .in_1(in_8), .in_7(in_2), .in_8(in_1), .in_9(demux_1_16_1_out_20), .in_10(demux_1_16_2_out_20),
    .in_2(in_7), .in_3(in_6), .in_4(in_5), .in_5(in_4), .in_6(in_3), .out_16(out_19), .out_17(out_19),
    .out_18(register_12_out_18), .out_11(out_19), .out_12(out_19), .out_13(out_19), .out_14(out_19),
    .out_15(out_19));
  register register_13 (
    .in_1(in_8), .in_7(in_2), .in_8(in_1), .in_9(demux_1_16_1_out_9), .in_10(demux_1_16_2_out_9),
    .in_2(in_7), .in_3(in_6), .in_4(in_5), .in_5(in_4), .in_6(in_3), .out_16(register_13_out_16),
    .out_17(register_13_out_17), .out_18(register_13_out_18), .out_11(register_13_out_11),
    .out_12(register_13_out_12), .out_13(register_13_out_13), .out_14(register_13_out_14),
    .out_15(register_13_out_15));
  register register_14 (
    .in_1(in_8), .in_7(in_2), .in_8(in_1), .in_9(demux_1_16_1_out_13), .in_10(demux_1_16_2_out_13),
    .in_2(in_7), .in_3(in_6), .in_4(in_5), .in_5(in_4), .in_6(in_3), .out_16(register_13_out_16),
    .out_17(register_13_out_17), .out_18(register_13_out_18), .out_11(register_13_out_11),
    .out_12(register_13_out_12), .out_13(register_13_out_13), .out_14(register_13_out_14),
    .out_15(register_13_out_15));
  register register_15 (
    .in_1(in_8), .in_7(in_2), .in_8(in_1), .in_9(demux_1_16_1_out_17), .in_10(demux_1_16_2_out_17),
    .in_2(in_7), .in_3(in_6), .in_4(in_5), .in_5(in_4), .in_6(in_3), .out_16(register_13_out_16),
    .out_17(register_13_out_17), .out_18(register_13_out_18), .out_11(register_13_out_11),
    .out_12(register_13_out_12), .out_13(register_13_out_13), .out_14(register_13_out_14),
    .out_15(register_13_out_15));
  register register_16 (
    .in_1(in_8), .in_7(in_2), .in_8(in_1), .in_9(demux_1_16_1_out_21), .in_10(demux_1_16_2_out_21),
    .in_2(in_7), .in_3(in_6), .in_4(in_5), .in_5(in_4), .in_6(in_3), .out_16(register_13_out_16),
    .out_17(register_13_out_17), .out_18(register_16_out_18), .out_11(register_13_out_11),
    .out_12(register_13_out_12), .out_13(register_13_out_13), .out_14(register_13_out_14),
    .out_15(register_13_out_15));
  Demux_1_16 demux_1_16_2 (
    .in_3(in_11), .in_2(in_10), .in_1(in_9), .in_4(in_12), .in_5(in_13), .out_7(demux_1_16_2_out_7),
    .out_8(demux_1_16_2_out_8), .out_9(demux_1_16_2_out_9), .out_10(demux_1_16_2_out_10),
    .out_11(demux_1_16_2_out_11), .out_12(demux_1_16_2_out_12), .out_13(demux_1_16_2_out_13),
    .out_14(demux_1_16_2_out_14), .out_15(demux_1_16_2_out_15), .out_16(demux_1_16_2_out_16),
    .out_17(demux_1_16_2_out_17), .out_18(demux_1_16_2_out_18), .out_19(demux_1_16_2_out_19),
    .out_20(demux_1_16_2_out_20), .out_21(demux_1_16_2_out_21), .out_6(demux_1_16_2_out_6));

  assign out_20 = out_19;
  assign out_21 = out_19;
  assign out_22 = out_19;
  assign out_23 = out_19;
  assign out_24 = out_19;
  assign out_25 = out_19;
  assign out_26 = out_19;
endmodule

module test (
  input  in_1,
  input  in_2,
  input  in_3,
  input  in_4,
  input  in_5,
  input  in_6,
  input  in_7,
  input  in_8,
  input  in_9,
  input  in_10,
  input  in_11,
  input  in_12,
  input  in_13,
  input  in_14
);

  sixteen_byte_reg sixteen_byte_reg_1 (
    .in_15(in_1), .in_16(in_2), .in_17(in_3), .in_18(in_4), .in_14(in_5), .in_9(in_4), .in_10(in_3),
    .in_11(in_2), .in_12(in_1), .in_13(in_14), .in_1(in_6), .in_2(in_7), .in_3(in_8), .in_4(in_9),
    .in_5(in_10), .in_6(in_11), .in_7(in_12), .in_8(in_13));  // open: out_22, out_23, out_24, out_25, out_26, out_19, out_20, out_21
endmodule

module side_or (
  input  in_1,
  input  in_2,
  input  in_3,
  input  in_4,
  input  in_5,
  input  in_6,
  input  in_7,
  input  in_8,
  input  in_9,
  input  in_10,
  input  in_11,
  input  in_12,
  input  in_13,
  input  in_14,
  input  in_15,
  input  in_16,
  output out_17,
  output out_18,
  output out_19,
  output out_20,
  output out_21,
  output out_22,
  output out_23,
  output out_24
);

  eight_bit_or eight_bit_or_1 (
    .in_1(in_8), .in_5(in_16), .in_9(in_4), .in_13(in_12), .in_2(in_7), .in_6(in_15), .in_10(in_3),
    .in_14(in_11), .in_3(in_6), .in_7(in_14), .in_11(in_2), .in_15(in_10), .in_4(in_5), .in_8(in_13),
    .in_12(in_1), .in_16(in_9), .out_17(out_24), .out_21(out_20), .out_18(out_23), .out_22(out_19),
    .out_19(out_22), .out_23(out_18), .out_20(out_21), .out_24(out_17));
endmodule
